# Fritzing sketch simon (saved by Fritzing 0.8.5b)
circuit board: 8.46667cm x 5.64444cm
breadboards: 1

parts:
  BAT1 = BC9VPC [package=bc9vpc]
  Part1 = Arduino Nano (Rev3.0)
  R1 = Resistor [tolerance=±5% resistance=220 package=THT]
  LED1 = LED - 5mm [color="Red (633nm)" package="5 mm [THT]"]
  S1 = Pushbutton [package="[THT]"]
  R2 = Resistor [tolerance=±5% resistance=220 package=THT]
  R3 = Resistor [tolerance=±5% resistance=220 package=THT]
  LED2 = LED - 5mm [color="Red (633nm)" package="5 mm [THT]"]
  S2 = Pushbutton [package="[THT]"]
  R4 = Resistor [tolerance=±5% resistance=220 package=THT]
  R5 = Resistor [tolerance=±5% resistance=220 package=THT]
  LED3 = LED - 5mm [color="Red (633nm)" package="5 mm [THT]"]
  S3 = Pushbutton [package="[THT]"]
  R6 = Resistor [tolerance=±5% resistance=220 package=THT]

nets (from the pcb view):
  N1: BAT1.V+, Part1.GND, LED1.cathode, R2.Pin_0, LED2.cathode, R4.Pin_0, LED3.cathode, R6.Pin_0
  N2: BAT1.V-, Part1.VIN
  N3: Part1.D4, Part1.5V, S2.Pin_3, S2.Pin_4, R4.Pin_1, S3.Pin_3, S3.Pin_4, R6.Pin_1
  N4: Part1.D6, S1.Pin_1, S1.Pin_2, R2.Pin_1
  N5: Part1.D10, R5.Pin_1
  N6: Part1.D11/MOSI, R3.Pin_1
  N7: Part1.D12/MISO, R1.Pin_1
  N8: R1.Pin_0, LED1.anode
  N9: S1.Pin_3, S2.Pin_1, S2.Pin_2, S3.Pin_1, S3.Pin_2
  N10: R3.Pin_0, LED2.anode
  N11: R5.Pin_0, LED3.anode
